// Logisim project first thingy.circ as structural Verilog: 4 circuits, main circuit main
module main (
  input  x,
  input  y
);

  wire and_1_out, and_2_out, not_1_out, not_2_out;

  not not_1 (not_1_out, x);
  not not_2 (not_2_out, y);
  and and_1 (and_1_out, not_1_out, x);
  and and_2 (and_2_out, y, not_2_out);
  // OR_Gate or_1 has open pins: in0=and_1_out, in4=and_2_out, out=open
endmodule

module full_adder (
  input  a,
  input  b,
  input  in_3,
  output out_4,
  output c
);

  wire and_1_out, and_2_out, or_1_out;

  or or_1 (or_1_out, a, b);
  and and_1 (and_1_out, a, b);
  or or_2 (out_4, or_1_out, in_3);
  and and_2 (and_2_out, or_1_out, in_3);
  or or_3 (c, and_2_out, and_1_out);
endmodule

// SR Latch
module sr_latch (
  input  s,
  input  r,
  output not_q,
  output q
);

  nor nor_1 (not_q, s, q);
  nor nor_2 (q, not_q, r);
endmodule

module d_latch (
  input  D,
  input  Strobe,
  output not_Q,
  output Q
);

  wire and_1_out, and_2_out, not_1_out, sr_latch_1_not_q, sr_latch_1_q;

  not not_1 (not_1_out, D);
  and and_1 (and_1_out, D, Strobe);
  and and_2 (and_2_out, not_1_out, Strobe);
  sr_latch sr_latch_1 (.s(and_1_out), .r(and_2_out), .not_q(sr_latch_1_not_q), .q(sr_latch_1_q));
endmodule
